// Logisim project A5Q1.circ as structural Verilog: 1 circuit, main circuit main
module main (
  input  in_1
);

  wire clock_1_out, not_1_out;
  wire [7:0] adder_1_out, ram_1_data, register_1_q;

  Clock clock_1 (.out(clock_1_out));
  Register register_1 (.D(adder_1_out), .en(in_1), .Q(register_1_q), .clk(clock_1_out), .clr(not_1_out));
  not not_1 (not_1_out, in_1);
  LED led_1 (.in(register_1_q[7]));
  Adder adder_1 (.a(8'h1), .b(register_1_q), .out(adder_1_out));  // open: cin, cout
  LED led_2 (.in(register_1_q[6]));
  LED led_3 (.in(register_1_q[3]));
  LED led_4 (.in(register_1_q[4]));
  LED led_5 (.in(register_1_q[5]));
  LED led_6 (.in(register_1_q[0]));
  LED led_7 (.in(register_1_q[2]));
  LED led_8 (.in(register_1_q[1]));
  Hex_Digit_Display hex_digit_display_1 (.value(ram_1_data[7:4]));  // open: dp
  RAM #(.bus("separate")) ram_1 (
    .addr(register_1_q), .din(8'h1), .data(ram_1_data), .clk(clock_1_out));  // open: str, sel, ld, clr
  Hex_Digit_Display hex_digit_display_2 (.value(ram_1_data[3:0]));  // open: dp
endmodule
