// Logisim project A5Q2.circ as structural Verilog: 1 circuit, main circuit main
module main (
  input  SUBTRACT,
  input  [7:0] in_2,
  input  [7:0] in_3
);

  wire and_1_out, and_2_out, and_3_out, and_4_out, and_5_out, and_6_out, and_7_out, and_8_out, not_1_out,
       xor_1_out, xor_2_out, xor_3_out, xor_4_out, xor_5_out, xor_6_out, xor_7_out;
  wire [7:0] adder_1_out;
  wire [7:1] xor_8_out;

  xor xor_1 (xor_1_out, in_2[2], SUBTRACT);
  xor xor_2 (xor_2_out, in_2[1], SUBTRACT);
  xor xor_3 (xor_3_out, in_2[5], SUBTRACT);
  xor xor_4 (xor_4_out, in_2[3], SUBTRACT);
  xor xor_5 (xor_5_out, in_2[4], SUBTRACT);
  xor xor_6 (xor_6_out, in_2[6], SUBTRACT);
  xor xor_7 (xor_7_out, in_2[7], SUBTRACT);
  and and_1 (and_1_out, SUBTRACT, not_1_out);
  not not_1 (not_1_out, in_2[0]);
  and and_2 (and_2_out, and_1_out, xor_2_out);
  and and_3 (and_3_out, and_2_out, xor_1_out);
  and and_4 (and_4_out, xor_4_out, and_3_out);
  and and_5 (and_5_out, and_4_out, xor_5_out);
  and and_6 (and_6_out, and_5_out, xor_3_out);
  and and_7 (and_7_out, xor_6_out, and_6_out);
  and and_8 (and_8_out, and_7_out, xor_7_out);
  xor xor_8 (xor_8_out[1], and_1_out, xor_2_out);
  xor xor_9 (xor_8_out[2], and_2_out, xor_1_out);
  xor xor_10 (xor_8_out[3], and_3_out, xor_4_out);
  xor xor_11 (xor_8_out[4], and_4_out, xor_5_out);
  xor xor_12 (xor_8_out[5], and_5_out, xor_3_out);
  xor xor_13 (xor_8_out[6], and_6_out, xor_6_out);
  xor xor_14 (xor_8_out[7], and_7_out, xor_7_out);
  Hex_Digit_Display hex_digit_display_1 (.value(adder_1_out[7:4]));  // open: dp
  Adder adder_1 (.a(in_3), .b({xor_8_out, in_2[0]}), .out(adder_1_out));  // open: cin, cout
  Hex_Digit_Display hex_digit_display_2 (.value(adder_1_out[3:0]));  // open: dp
endmodule
