// Logisim project A5Q3.circ as structural Verilog: 4 circuits, main circuit main
module main (
  input  in_1
);

  wire _00_out, _01_out, _10_out, _11_out, clock_1_out, not_1_out, not_2_out, not_3_out, not_4_out, or_1_out,
       or_2_out;
  wire [1:0] multiplexer_1_out;
  wire [3:0] pc_1_result, pc_1_result_2;
  wire [7:0] alu_1_out_4, multiplexer_2_out, multiplexer_3_out, ram_1_data, registers_1_readdata1,
       registers_1_readdata2;

  Hex_Digit_Display hex_digit_display_1 (.value(pc_1_result_2));  // open: dp
  Hex_Digit_Display hex_digit_display_2 (.value(pc_1_result));  // open: dp
  Clock clock_1 (.out(clock_1_out));
  PC pc_1 (.ON_OFF(in_1), .Clock(clock_1_out), .Result({pc_1_result, pc_1_result_2}));
  or or_1 (or_1_out, _00_out, _01_out);
  Multiplexer #(.width(2), .enable("false")) multiplexer_1 (
    .in0(pc_1_result[1:0]), .in1(pc_1_result_2[1:0]), .out(multiplexer_1_out), .sel(or_1_out));
  or or_2 (or_2_out, _11_out, or_1_out);
  Registers registers_1 (
    .WriteData(multiplexer_2_out), .WriteReg(multiplexer_1_out), .Write(or_2_out), .Clock(clock_1_out),
    .ReadData1(registers_1_readdata1), .ReadReg1(pc_1_result_2[3:2]), .ReadData2(registers_1_readdata2),
    .ReadReg2(pc_1_result[1:0]));
  Multiplexer #(.width(8), .enable("false")) multiplexer_2 (
    .in0(ram_1_data), .in1(alu_1_out_4), .out(multiplexer_2_out), .sel(or_1_out));
  not not_1 (not_1_out, pc_1_result[2]);
  not not_2 (not_2_out, pc_1_result[3]);
  not not_3 (not_3_out, pc_1_result[3]);
  and _00 (_00_out, not_2_out, not_1_out);
  ALU alu_1 (.in_2(registers_1_readdata2), .in_3(registers_1_readdata1), .SUBTRACT(_00_out), .out_4(alu_1_out_4));
  not not_4 (not_4_out, pc_1_result[2]);
  and _10 (_10_out, pc_1_result[3], not_4_out);
  and _11 (_11_out, pc_1_result[3], pc_1_result[2]);
  and _01 (_01_out, not_3_out, pc_1_result[2]);
  Multiplexer #(.width(8), .enable("false")) multiplexer_3 (
    .in0(ram_1_data), .in1(registers_1_readdata2), .out(multiplexer_3_out), .sel(_10_out));
  RAM #(.bus("separate")) ram_1 (
    .addr({4'b0000, pc_1_result_2}), .din(multiplexer_3_out), .data(ram_1_data), .clk(clock_1_out));  // open: str, sel, ld, clr

  // Notes on the sheet:
  //   OPCODE
endmodule

module PC (
  input  ON_OFF,
  input  Clock,
  output [7:0] Result
);

  wire not_1_out;
  wire [7:0] adder_1_out, register_1_q;

  Register register_1 (.D(adder_1_out), .en(ON_OFF), .Q(register_1_q), .clk(Clock), .clr(not_1_out));
  not not_1 (not_1_out, ON_OFF);
  Adder adder_1 (.a(8'h1), .b(register_1_q), .out(adder_1_out));  // open: cin, cout
  LED led_1 (.in(register_1_q[7]));
  LED led_2 (.in(register_1_q[4]));
  LED led_3 (.in(register_1_q[6]));
  LED led_4 (.in(register_1_q[5]));
  LED led_5 (.in(register_1_q[3]));
  LED led_6 (.in(register_1_q[1]));
  LED led_7 (.in(register_1_q[0]));
  LED led_8 (.in(register_1_q[2]));
  ROM rom_1 (.addr(register_1_q), .data(Result));  // open: sel
  Hex_Digit_Display hex_digit_display_1 (.value(Result[3:0]));  // open: dp
  Hex_Digit_Display hex_digit_display_2 (.value(Result[7:4]));  // open: dp

  // Notes on the sheet:
  //   contents of rom_1 (hex, n*v repeats v):
  //   c0 41 91 51 92 51 93 5 94 5 95 86
endmodule

// REGs
module Registers (
  input  [7:0] WriteData,
  input  [1:0] WriteReg,
  input  [1:0] ReadReg1,
  input  [1:0] ReadReg2,
  input  Write,
  input  Clock,
  output [7:0] ReadData1,
  output [7:0] ReadData2
);

  wire and_1_out, and_2_out, and_3_out, and_4_out, decoder_1_out0, decoder_1_out1, decoder_1_out2,
       decoder_1_out3;
  wire [7:0] multiplexer_1_out, multiplexer_2_out, multiplexer_3_out, multiplexer_4_out, register_1_q,
       register_2_q, register_3_q, register_4_q;

  Decoder #(.select(2), .enable("false")) decoder_1 (
    .out0(decoder_1_out0), .out1(decoder_1_out1), .out2(decoder_1_out2), .out3(decoder_1_out3), .sel(WriteReg));
  and and_1 (and_1_out, decoder_1_out0, Write);
  and and_2 (and_2_out, decoder_1_out1, Write);
  and and_3 (and_3_out, decoder_1_out2, Write);
  and and_4 (and_4_out, decoder_1_out3, Write);
  Multiplexer #(.width(8), .enable("false")) multiplexer_1 (
    .in0(register_1_q), .in1(WriteData), .out(multiplexer_1_out), .sel(and_1_out));
  Multiplexer #(.width(8), .enable("false")) multiplexer_2 (
    .in0(register_2_q), .in1(WriteData), .out(multiplexer_2_out), .sel(and_2_out));
  Multiplexer #(.width(8), .enable("false")) multiplexer_3 (
    .in0(register_3_q), .in1(WriteData), .out(multiplexer_3_out), .sel(and_3_out));
  Multiplexer #(.width(8), .enable("false")) multiplexer_4 (
    .in0(register_4_q), .in1(WriteData), .out(multiplexer_4_out), .sel(and_4_out));
  Register register_1 (.D(multiplexer_1_out), .Q(register_1_q), .clk(Clock));  // open: en, clr
  Register register_2 (.D(multiplexer_2_out), .Q(register_2_q), .clk(Clock));  // open: en, clr
  Register register_3 (.D(multiplexer_3_out), .Q(register_3_q), .clk(Clock));  // open: en, clr
  Register register_4 (.D(multiplexer_4_out), .Q(register_4_q), .clk(Clock));  // open: en, clr
  Multiplexer #(.select(2), .width(8), .enable("false")) multiplexer_5 (
    .in0(register_1_q), .in1(register_2_q), .in2(register_3_q), .in3(register_4_q), .out(ReadData1),
    .sel(ReadReg1));
  Multiplexer #(.select(2), .width(8), .enable("false")) multiplexer_6 (
    .in0(register_1_q), .in1(register_2_q), .in2(register_3_q), .in3(register_4_q), .out(ReadData2),
    .sel(ReadReg2));

  // Notes on the sheet:
  //   Register File 8x8-bits
endmodule

module ALU (
  input  SUBTRACT,
  input  [7:0] in_2,
  input  [7:0] in_3,
  output [7:0] out_4
);

  wire and_1_out, and_2_out, and_3_out, and_4_out, and_5_out, and_6_out, and_7_out, and_8_out, not_1_out,
       xor_1_out, xor_2_out, xor_3_out, xor_4_out, xor_5_out, xor_6_out, xor_7_out;
  wire [7:1] xor_8_out;

  xor xor_1 (xor_1_out, in_2[1], SUBTRACT);
  xor xor_2 (xor_2_out, in_2[3], SUBTRACT);
  xor xor_3 (xor_3_out, in_2[2], SUBTRACT);
  xor xor_4 (xor_4_out, in_2[6], SUBTRACT);
  xor xor_5 (xor_5_out, in_2[4], SUBTRACT);
  xor xor_6 (xor_6_out, in_2[5], SUBTRACT);
  not not_1 (not_1_out, in_2[0]);
  xor xor_7 (xor_7_out, in_2[7], SUBTRACT);
  and and_1 (and_1_out, SUBTRACT, not_1_out);
  and and_2 (and_2_out, and_1_out, xor_1_out);
  and and_3 (and_3_out, and_2_out, xor_3_out);
  and and_4 (and_4_out, xor_2_out, and_3_out);
  and and_5 (and_5_out, and_4_out, xor_5_out);
  and and_6 (and_6_out, and_5_out, xor_6_out);
  and and_7 (and_7_out, xor_4_out, and_6_out);
  and and_8 (and_8_out, and_7_out, xor_7_out);
  xor xor_8 (xor_8_out[1], and_1_out, xor_1_out);
  xor xor_9 (xor_8_out[2], and_2_out, xor_3_out);
  xor xor_10 (xor_8_out[3], and_3_out, xor_2_out);
  xor xor_11 (xor_8_out[4], and_4_out, xor_5_out);
  xor xor_12 (xor_8_out[5], and_5_out, xor_6_out);
  xor xor_13 (xor_8_out[6], and_6_out, xor_4_out);
  xor xor_14 (xor_8_out[7], and_7_out, xor_7_out);
  Adder adder_1 (.a(in_3), .b({xor_8_out, in_2[0]}), .out(out_4));  // open: cin, cout
endmodule
